// Logisim project EP3.circ as structural Verilog: 9 circuits, main circuit Verifica_Sinal
module main (
  input  OP,
  input  [7:0] A,
  input  [7:0] B,
  output out_4,
  output out_5,
  output out_6,
  output out_7,
  output A___B,
  output A___0,
  output out_10,
  output out_11,
  output [7:0] out_12
);

  ULA ula_1 (
    .Controle(OP), .A(A), .B(B), .Overflow_Sem_Sinal(out_4), .Overflow_Com_Sinal(out_5), .C0(out_6),
    .C1(out_7), .C2(A___B), .C3(A___0), .C4(out_10), .C5(out_11), .Resultado(out_12));

  // Notes on the sheet:
  //   NUSP 14600541
  //   Nathália Yukimi Uchiyama Tsuno
  //   Simulador de ULA
  //   Overflow Sem Sinal
  //   Overflow Com Sinal
  //   A > B (Sem Sinal)
  //   A < B (Sem Sinal)
  //   A > B (Com Sinal)
  //   A < B (Com Sinal)
  //   Resultado
endmodule

module Comparabits (
  input  Controle,
  input  digito_a,
  input  digito_b,
  output out_4,
  output out_5,
  output out_6
);

  wire not_1_out, not_2_out, not_3_out, xor_1_out;

  xor xor_1 (xor_1_out, digito_a, digito_b);
  not not_1 (not_1_out, xor_1_out);
  not not_2 (not_2_out, digito_a);
  not not_3 (not_3_out, digito_b);
  and and_1 (out_4, Controle, not_1_out);
  and and_2 (out_5, not_2_out, Controle, digito_b);
  and and_3 (out_6, digito_a, Controle, not_3_out);

  // Notes on the sheet:
  //   digito_a = digito_b
  //   digito_a < digito_b
  //   digito_a > digito_b
endmodule

module Circuito_Comparador (
  input  Controle,
  input  [7:0] A,
  input  [7:0] B,
  output out_4,
  output out_5,
  output out_6
);

  wire comparabits0_out_4, comparabits0_out_5, comparabits0_out_6, comparabits1_out_4, comparabits1_out_5,
       comparabits1_out_6, comparabits2_out_4, comparabits2_out_5, comparabits2_out_6, comparabits3_out_4,
       comparabits3_out_5, comparabits3_out_6, comparabits4_out_4, comparabits4_out_5, comparabits4_out_6,
       comparabits5_out_4, comparabits5_out_5, comparabits5_out_6, comparabits6_out_4, comparabits6_out_5,
       comparabits6_out_6, comparabits7_out_5, comparabits7_out_6;

  Comparabits comparabits0 (
    .Controle(Controle), .digito_a(A[7]), .digito_b(B[7]), .out_4(comparabits0_out_4),
    .out_5(comparabits0_out_5), .out_6(comparabits0_out_6));
  Comparabits comparabits1 (
    .Controle(comparabits0_out_4), .digito_a(A[6]), .digito_b(B[6]), .out_4(comparabits1_out_4),
    .out_5(comparabits1_out_5), .out_6(comparabits1_out_6));
  Comparabits comparabits2 (
    .Controle(comparabits1_out_4), .digito_a(A[5]), .digito_b(B[5]), .out_4(comparabits2_out_4),
    .out_5(comparabits2_out_5), .out_6(comparabits2_out_6));
  Comparabits comparabits3 (
    .Controle(comparabits2_out_4), .digito_a(A[4]), .digito_b(B[4]), .out_4(comparabits3_out_4),
    .out_5(comparabits3_out_5), .out_6(comparabits3_out_6));
  Comparabits comparabits4 (
    .Controle(comparabits3_out_4), .digito_a(A[3]), .digito_b(B[3]), .out_4(comparabits4_out_4),
    .out_5(comparabits4_out_5), .out_6(comparabits4_out_6));
  Comparabits comparabits5 (
    .Controle(comparabits4_out_4), .digito_a(A[2]), .digito_b(B[2]), .out_4(comparabits5_out_4),
    .out_5(comparabits5_out_5), .out_6(comparabits5_out_6));
  Comparabits comparabits6 (
    .Controle(comparabits5_out_4), .digito_a(A[1]), .digito_b(B[1]), .out_4(comparabits6_out_4),
    .out_5(comparabits6_out_5), .out_6(comparabits6_out_6));
  Comparabits comparabits7 (
    .Controle(comparabits6_out_4), .digito_a(A[0]), .digito_b(B[0]), .out_4(out_6),
    .out_5(comparabits7_out_5), .out_6(comparabits7_out_6));
  or or_1 (out_4, comparabits0_out_5, comparabits1_out_5, comparabits2_out_5, comparabits3_out_5, comparabits4_out_5, comparabits5_out_5, comparabits6_out_5, comparabits7_out_5);
  or or_2 (out_5, comparabits0_out_6, comparabits1_out_6, comparabits2_out_6, comparabits3_out_6, comparabits4_out_6, comparabits5_out_6, comparabits6_out_6, comparabits7_out_6);

  // Notes on the sheet:
  //   A < B
  //   A > B
  //   A == B
endmodule

module Comparador (
  input  [7:0] A,
  input  [7:0] B,
  output C0,
  output C1,
  output C2,
  output C3,
  output C4,
  output C5
);

  wire circuito_comparador_1_out_4, circuito_comparador_1_out_5, verifica_sinal_1_out_3,
       verifica_sinal_1_out_4, verifica_sinal_1_out_5;

  Verifica_Sinal verifica_sinal_1 (
    .digito_a(A[7]), .digito_b(B[7]), .out_3(verifica_sinal_1_out_3), .out_4(verifica_sinal_1_out_4),
    .out_5(verifica_sinal_1_out_5));
  Circuito_Comparador circuito_comparador_1 (
    .Controle(verifica_sinal_1_out_3), .A(A), .B(B), .out_4(circuito_comparador_1_out_4),
    .out_5(circuito_comparador_1_out_5), .out_6(C2));
  nor nor_1 (C3, A[0], A[1], A[2], A[3], A[4], A[5], A[6], A[7]);
  xor xor_1 (C0, circuito_comparador_1_out_5, verifica_sinal_1_out_5);
  xor xor_2 (C1, circuito_comparador_1_out_4, verifica_sinal_1_out_4);
  xor xor_3 (C4, circuito_comparador_1_out_5, verifica_sinal_1_out_4);
  xor xor_4 (C5, circuito_comparador_1_out_4, verifica_sinal_1_out_5);
endmodule

module Verifica_Sinal (
  input  digito_a,
  input  digito_b,
  output out_3,
  output out_4,
  output out_5
);

  wire not_1_out, not_2_out, xor_1_out;

  not not_1 (not_1_out, digito_a);
  not not_2 (not_2_out, digito_b);
  xor xor_1 (xor_1_out, digito_a, digito_b);
  and and_1 (out_4, not_1_out, digito_b);
  and and_2 (out_5, digito_a, not_2_out);
  not not_3 (out_3, xor_1_out);

  // Notes on the sheet:
  //   digito_a = digito_b
  //   digito_a < digito_b
  //   digito_a > digito_b
endmodule

module Somabits (
  input  carry_in,
  input  digito_a,
  input  digito_b,
  output s,
  output carry_out
);

  wire and_1_out, and_2_out, and_3_out, and_4_out, not_1_out, xnor_1_out, xor_1_out;

  not not_1 (not_1_out, carry_in);
  xor xor_1 (xor_1_out, digito_a, digito_b);
  xnor xnor_1 (xnor_1_out, digito_a, digito_b);
  and and_1 (and_1_out, not_1_out, xor_1_out);
  and and_2 (and_2_out, carry_in, xnor_1_out);
  and and_3 (and_3_out, carry_in, xor_1_out);
  and and_4 (and_4_out, digito_a, digito_b);
  or or_1 (s, and_1_out, and_2_out);
  or or_2 (carry_out, and_3_out, and_4_out);
endmodule

module Somador (
  input  OP,
  input  [7:0] A,
  input  [7:0] B,
  output [7:0] Resultado,
  output Carry_6,
  output Carry_7
);

  wire somabits_1_carry_out, somabits_2_carry_out, somabits_3_carry_out, somabits_4_carry_out,
       somabits_5_carry_out, somabits_6_carry_out;

  Somabits somabits_1 (
    .carry_in(OP), .digito_a(A[0]), .digito_b(B[0]), .s(Resultado[0]), .carry_out(somabits_1_carry_out));
  Somabits somabits_2 (
    .carry_in(somabits_1_carry_out), .digito_a(A[1]), .digito_b(B[1]), .s(Resultado[1]),
    .carry_out(somabits_2_carry_out));
  Somabits somabits_3 (
    .carry_in(somabits_2_carry_out), .digito_a(A[2]), .digito_b(B[2]), .s(Resultado[2]),
    .carry_out(somabits_3_carry_out));
  Somabits somabits_4 (
    .carry_in(somabits_3_carry_out), .digito_a(A[3]), .digito_b(B[3]), .s(Resultado[3]),
    .carry_out(somabits_4_carry_out));
  Somabits somabits_5 (
    .carry_in(somabits_4_carry_out), .digito_a(A[4]), .digito_b(B[4]), .s(Resultado[4]),
    .carry_out(somabits_5_carry_out));
  Somabits somabits_6 (
    .carry_in(somabits_5_carry_out), .digito_a(A[5]), .digito_b(B[5]), .s(Resultado[5]),
    .carry_out(somabits_6_carry_out));
  Somabits somabits_7 (
    .carry_in(somabits_6_carry_out), .digito_a(A[6]), .digito_b(B[6]), .s(Resultado[6]), .carry_out(Carry_6));
  Somabits somabits_8 (.carry_in(Carry_6), .digito_a(A[7]), .digito_b(B[7]), .s(Resultado[7]), .carry_out(Carry_7));
endmodule

module Inversor_de_Sinal (
  input  OP,
  input  [7:0] Numero,
  output [7:0] Numero_barrado
);

  xor xor_1 (Numero_barrado[0], OP, Numero[0]);
  xor xor_2 (Numero_barrado[1], OP, Numero[1]);
  xor xor_3 (Numero_barrado[2], OP, Numero[2]);
  xor xor_4 (Numero_barrado[3], OP, Numero[3]);
  xor xor_5 (Numero_barrado[4], OP, Numero[4]);
  xor xor_6 (Numero_barrado[5], OP, Numero[5]);
  xor xor_7 (Numero_barrado[6], OP, Numero[6]);
  xor xor_8 (Numero_barrado[7], OP, Numero[7]);
endmodule

module ULA (
  input  Controle,
  input  [7:0] A,
  input  [7:0] B,
  output Overflow_Sem_Sinal,
  output Overflow_Com_Sinal,
  output C0,
  output C1,
  output C2,
  output C3,
  output C4,
  output C5,
  output [7:0] Resultado
);

  wire somador_1_carry_6, somador_1_carry_7;
  wire [7:0] inversor_de_sinal_1_numero_barrado;

  Inversor_de_Sinal inversor_de_sinal_1 (
    .OP(Controle), .Numero(B), .Numero_barrado(inversor_de_sinal_1_numero_barrado));
  Somador somador_1 (
    .OP(Controle), .A(A), .B(inversor_de_sinal_1_numero_barrado), .Resultado(Resultado),
    .Carry_6(somador_1_carry_6), .Carry_7(somador_1_carry_7));
  Comparador comparador_1 (.A(A), .B(B), .C0(C0), .C1(C1), .C2(C2), .C3(C3), .C4(C4), .C5(C5));
  xor xor_1 (Overflow_Sem_Sinal, Controle, somador_1_carry_7);
  xor xor_2 (Overflow_Com_Sinal, somador_1_carry_6, somador_1_carry_7);

  // Notes on the sheet:
  //   A > B 
  //   A < B
  //   A == B
  //   A == 0
  //   A > B (Considerando o Sinal)
  //   A < B (Considerando o Sinal)
endmodule
